// Logisim project ping-pong.circ as structural Verilog
// 0xd
module movePoint (
);

  wire and_1_out, and_2_out, bot_enabled, comp_y_cord_1_out_4, comp_y_cord_2_out_4, comparator_1_eq,
       comparator_2_eq, comparator_3_eq, comparator_4_eq, comparator_5_eq, comparator_6_eq, comparator_7_eq,
       comparator_8_eq, comparator_9_eq, comparator_10_eq, comparator_11_eq, d_ff_2_q, fail1, fail2, isDown,
       kpower, lose, not_1_out, not_2_out, not_3_out, not_4_out, not_5_out, not_6_out, or_3_out, or_5_out,
       or_6_out, or_7_out, or_8_out, pause, power, pull_resistor_2_node, restart, swap_x_direction_left_wall,
       swap_x_direction_right_wall, transistor_1_out, undriven, undriven_3, undriven_4;
  wire [3:0] counter_1_q, counter_3_q, counter_4_q, undriven_2;
  wire [4:0] dmx_x_cord;
  wire [6:0] keyboard;
  wire [7:0] counter_6_q, counter_7_q, multiplexer_34_out;
  wire [11:0] p1_score, p2_score;
  wire [14:1] decoder_3_out0, middle_rocket_pixel_left;
  wire [15:0] bot, cord1, cord2, demultiplexer_1_out0, demultiplexer_1_out1, demultiplexer_1_out3,
       demultiplexer_1_out4, demultiplexer_1_out5, demultiplexer_1_out6, demultiplexer_1_out7,
       demultiplexer_1_out8, demultiplexer_1_out9, demultiplexer_1_out10, demultiplexer_1_out11,
       demultiplexer_1_out12, demultiplexer_1_out13, demultiplexer_1_out14, demultiplexer_1_out15,
       demultiplexer_1_out16, demultiplexer_1_out17, demultiplexer_1_out18, demultiplexer_1_out19,
       demultiplexer_1_out20, demultiplexer_1_out21, demultiplexer_1_out22, demultiplexer_1_out23,
       demultiplexer_1_out24, demultiplexer_1_out25, demultiplexer_1_out26, demultiplexer_1_out27,
       demultiplexer_1_out28, demultiplexer_1_out30, demultiplexer_1_out31, dmx_y_cord, multiplexer_1_out,
       multiplexer_2_out, multiplexer_3_out, multiplexer_4_out, multiplexer_5_out, multiplexer_6_out,
       multiplexer_7_out, multiplexer_8_out, multiplexer_9_out, multiplexer_10_out, multiplexer_11_out,
       multiplexer_12_out, multiplexer_13_out, multiplexer_14_out, multiplexer_15_out, multiplexer_16_out,
       multiplexer_17_out, multiplexer_18_out, multiplexer_19_out, multiplexer_20_out, multiplexer_21_out,
       multiplexer_22_out, multiplexer_23_out, multiplexer_24_out, multiplexer_25_out, multiplexer_26_out,
       multiplexer_27_out, multiplexer_28_out, multiplexer_29_out, multiplexer_30_out, multiplexer_31_out,
       multiplexer_32_out, or_1_out, or_2_out, player1, player2, racket2, shifter_1_out, shifter_2_out,
       shifter_3_out, shifter_4_out, shifter_5_out, shifter_6_out;

  Multiplexer #(.width(16)) multiplexer_1 (
    .in0(demultiplexer_1_out0), .in1({16{1'b0}}), .out(multiplexer_1_out), .sel(pause));  // open: en
  Hex_Digit_Display hex_digit_display_1 (.value(p1_score[7:4]));  // open: dp
  Hex_Digit_Display hex_digit_display_2 (.value(p1_score[11:8]));  // open: dp
  Multiplexer #(.width(16)) multiplexer_2 (
    .in0(or_1_out), .in1({16{1'b0}}), .out(multiplexer_2_out), .sel(pause));  // open: en
  Hex_Digit_Display hex_digit_display_3 (.value(p1_score[3:0]));  // open: dp
  DotMatrix #(.matrixcols(32), .matrixrows(16)) dotmatrix_1 (
    .col0(multiplexer_1_out), .col1(multiplexer_2_out), .col2(multiplexer_3_out), .col3(multiplexer_4_out),
    .col4(multiplexer_5_out), .col5(multiplexer_6_out), .col6(multiplexer_7_out), .col7(multiplexer_8_out),
    .col8(multiplexer_9_out), .col9(multiplexer_10_out), .col10(multiplexer_11_out),
    .col11(multiplexer_12_out), .col12(multiplexer_14_out), .col13(multiplexer_13_out),
    .col14(multiplexer_15_out), .col15(multiplexer_16_out), .col16(multiplexer_18_out),
    .col17(multiplexer_17_out), .col18(multiplexer_19_out), .col19(multiplexer_20_out),
    .col20(multiplexer_22_out), .col21(multiplexer_21_out), .col22(multiplexer_23_out),
    .col23(multiplexer_24_out), .col24(multiplexer_26_out), .col25(multiplexer_25_out),
    .col26(multiplexer_27_out), .col27(multiplexer_28_out), .col28(multiplexer_30_out),
    .col29(multiplexer_29_out), .col30(multiplexer_31_out), .col31(multiplexer_32_out));
  Multiplexer #(.width(16)) multiplexer_3 (
    .in0(cord1), .in1({16{1'b0}}), .out(multiplexer_3_out), .sel(pause));  // open: en
  assign or_1_out = player1 | demultiplexer_1_out1;  // OR_Gate or_1, 16 bits wide
  Multiplexer #(.width(16)) multiplexer_4 (
    .in0(demultiplexer_1_out3), .in1(16'h1ffc), .out(multiplexer_4_out), .sel(pause));  // open: en
  Multiplexer #(.width(16)) multiplexer_5 (
    .in0(demultiplexer_1_out4), .in1(16'h1100), .out(multiplexer_5_out), .sel(pause));  // open: en
  Multiplexer #(.width(16)) multiplexer_6 (
    .in0(demultiplexer_1_out5), .in1(16'h1100), .out(multiplexer_6_out), .sel(pause));  // open: en
  Demultiplexer #(.select(5), .width(16)) demultiplexer_1 (
    .out0(demultiplexer_1_out0), .out1(demultiplexer_1_out1), .out2(cord1), .out3(demultiplexer_1_out3),
    .out4(demultiplexer_1_out4), .out5(demultiplexer_1_out5), .out6(demultiplexer_1_out6),
    .out7(demultiplexer_1_out7), .out8(demultiplexer_1_out8), .out9(demultiplexer_1_out9),
    .out10(demultiplexer_1_out10), .out11(demultiplexer_1_out11), .out12(demultiplexer_1_out12),
    .out13(demultiplexer_1_out13), .out14(demultiplexer_1_out14), .out15(demultiplexer_1_out15),
    .out16(demultiplexer_1_out16), .out17(demultiplexer_1_out17), .out18(demultiplexer_1_out18),
    .out19(demultiplexer_1_out19), .out20(demultiplexer_1_out20), .out21(demultiplexer_1_out21),
    .out22(demultiplexer_1_out22), .out23(demultiplexer_1_out23), .out24(demultiplexer_1_out24),
    .out25(demultiplexer_1_out25), .out26(demultiplexer_1_out26), .out27(demultiplexer_1_out27),
    .out28(demultiplexer_1_out28), .out29(cord2), .out30(demultiplexer_1_out30),
    .out31(demultiplexer_1_out31), .in(dmx_y_cord), .sel(dmx_x_cord));  // open: en
  Multiplexer #(.width(16)) multiplexer_7 (
    .in0(demultiplexer_1_out6), .in1(16'h1100), .out(multiplexer_7_out), .sel(pause));  // open: en
  Multiplexer #(.width(16)) multiplexer_8 (
    .in0(demultiplexer_1_out7), .in1(16'he00), .out(multiplexer_8_out), .sel(pause));  // open: en
  assign or_2_out = racket2 | demultiplexer_1_out30;  // OR_Gate or_2, 16 bits wide
  Hex_Digit_Display hex_digit_display_4 (.value(p2_score[7:4]));  // open: dp
  Hex_Digit_Display hex_digit_display_5 (.value(p2_score[11:8]));  // open: dp
  Multiplexer #(.width(16)) multiplexer_9 (
    .in0(demultiplexer_1_out8), .in1(16'hfc), .out(multiplexer_9_out), .sel(pause));  // open: en
  Multiplexer #(.width(16)) multiplexer_10 (
    .in0(demultiplexer_1_out9), .in1(16'h110), .out(multiplexer_10_out), .sel(pause));  // open: en
  Hex_Digit_Display hex_digit_display_6 (.value(p2_score[3:0]));  // open: dp
  Multiplexer #(.width(16)) multiplexer_11 (
    .in0(demultiplexer_1_out10), .in1(16'h110), .out(multiplexer_11_out), .sel(pause));  // open: en
  Multiplexer #(.width(16)) multiplexer_12 (
    .in0(demultiplexer_1_out11), .in1(16'hfc), .out(multiplexer_12_out), .sel(pause));  // open: en
  Keyboard #(.buflen(1)) keyboard_1 (.clk(kpower), .data(keyboard));  // open: re, clr, avail
  Multiplexer #(.width(16)) multiplexer_13 (
    .in0(demultiplexer_1_out13), .in1(16'h1f8), .out(multiplexer_13_out), .sel(pause));  // open: en
  Multiplexer #(.width(16)) multiplexer_14 (
    .in0(demultiplexer_1_out12), .in1({16{1'b0}}), .out(multiplexer_14_out), .sel(pause));  // open: en
  Multiplexer #(.width(16)) multiplexer_15 (
    .in0(demultiplexer_1_out14), .in1(16'h4), .out(multiplexer_15_out), .sel(pause));  // open: en
  Multiplexer #(.width(16)) multiplexer_16 (
    .in0(demultiplexer_1_out15), .in1(16'h4), .out(multiplexer_16_out), .sel(pause));  // open: en
  Multiplexer #(.width(16)) multiplexer_17 (
    .in0(demultiplexer_1_out17), .in1({16{1'b0}}), .out(multiplexer_17_out), .sel(pause));  // open: en
  Multiplexer #(.width(16)) multiplexer_18 (
    .in0(demultiplexer_1_out16), .in1(16'h1f8), .out(multiplexer_18_out), .sel(pause));  // open: en
  Multiplexer #(.width(16)) multiplexer_19 (
    .in0(demultiplexer_1_out18), .in1(16'hc8), .out(multiplexer_19_out), .sel(pause));  // open: en
  Multiplexer #(.width(16)) multiplexer_20 (
    .in0(demultiplexer_1_out19), .in1(16'h124), .out(multiplexer_20_out), .sel(pause));  // open: en
  Multiplexer #(.width(16)) multiplexer_21 (
    .in0(demultiplexer_1_out21), .in1(16'h98), .out(multiplexer_21_out), .sel(pause));  // open: en
  Multiplexer #(.width(16)) multiplexer_22 (
    .in0(demultiplexer_1_out20), .in1(16'h124), .out(multiplexer_22_out), .sel(pause));  // open: en
  Multiplexer #(.width(16)) multiplexer_23 (
    .in0(demultiplexer_1_out22), .in1({16{1'b0}}), .out(multiplexer_23_out), .sel(pause));  // open: en
  Multiplexer #(.width(16)) multiplexer_24 (
    .in0(demultiplexer_1_out23), .in1(16'h1fc), .out(multiplexer_24_out), .sel(pause));  // open: en
  Multiplexer #(.width(16)) multiplexer_25 (
    .in0(demultiplexer_1_out25), .in1(16'h124), .out(multiplexer_25_out), .sel(pause));  // open: en
  Multiplexer #(.width(16)) multiplexer_26 (
    .in0(demultiplexer_1_out24), .in1(16'h124), .out(multiplexer_26_out), .sel(pause));  // open: en
  Multiplexer #(.width(16)) multiplexer_27 (
    .in0(demultiplexer_1_out26), .in1(16'h124), .out(multiplexer_27_out), .sel(pause));  // open: en
  Multiplexer #(.width(16)) multiplexer_28 (
    .in0(demultiplexer_1_out27), .in1({16{1'b0}}), .out(multiplexer_28_out), .sel(pause));  // open: en
  Multiplexer #(.width(16)) multiplexer_29 (
    .in0(cord2), .in1({16{1'b0}}), .out(multiplexer_29_out), .sel(pause));  // open: en
  Multiplexer #(.width(16)) multiplexer_30 (
    .in0(demultiplexer_1_out28), .in1(16'h1fe4), .out(multiplexer_30_out), .sel(pause));  // open: en
  Multiplexer #(.width(16)) multiplexer_31 (
    .in0(or_2_out), .in1({16{1'b0}}), .out(multiplexer_31_out), .sel(pause));  // open: en
  Multiplexer #(.width(16)) multiplexer_32 (
    .in0(demultiplexer_1_out31), .in1({16{1'b0}}), .out(multiplexer_32_out), .sel(pause));  // open: en
  D_Flip_Flop d_ff_1 (.Q(isDown), .preset(dmx_y_cord[15]), .reset(dmx_y_cord[0]));  // open: clk, D, Qn, en
  Counter #(.width(4), .max('hf)) counter_1 (
    .load(isDown), .Q(counter_1_q), .clk(power));  // open: D, count, carry, clr
  Multiplexer #(.width(16)) multiplexer_33 (.in0(player2), .in1(bot), .out(racket2), .sel(bot_enabled));  // open: en
  // Probe on keyboard
  // Probe on keyboard
  // Probe on keyboard
  // Probe on keyboard
  Decoder #(.select(4)) decoder_1 (
    .out0(dmx_y_cord[0]), .out1(dmx_y_cord[1]), .out2(dmx_y_cord[2]), .out3(dmx_y_cord[3]),
    .out4(dmx_y_cord[4]), .out5(dmx_y_cord[5]), .out6(dmx_y_cord[6]), .out7(dmx_y_cord[7]),
    .out8(dmx_y_cord[8]), .out9(dmx_y_cord[9]), .out10(dmx_y_cord[10]), .out11(dmx_y_cord[11]),
    .out12(dmx_y_cord[12]), .out13(dmx_y_cord[13]), .out14(dmx_y_cord[14]), .out15(dmx_y_cord[15]),
    .sel(counter_1_q));  // open: en
  // Probe on d_ff_2_q
  D_Flip_Flop d_ff_2 (
    .Q(d_ff_2_q), .preset(swap_x_direction_right_wall), .reset(swap_x_direction_left_wall));  // open: clk, D, Qn, en
  Counter #(.width(5), .max('h1f)) counter_2 (
    .load(d_ff_2_q), .Q(dmx_x_cord), .clk(power), .clr(or_3_out));  // open: D, count, carry
  Shifter #(.width(16)) shifter_1 (.in(dmx_y_cord), .\dist (4'b0001), .out(shifter_1_out));
  Shifter #(.width(16), .shift("lr")) shifter_2 (.in(dmx_y_cord), .\dist (4'b0001), .out(shifter_2_out));
  Comparator #(.width(7)) comparator_1 (.a(keyboard), .b(7'b1110111), .eq(comparator_1_eq));  // open: gt, lt
  Comparator #(.width(7)) comparator_2 (.a(keyboard), .b(7'b1110011), .eq(comparator_2_eq));  // open: gt, lt
  Comparator #(.width(7)) comparator_3 (.a(keyboard), .b(7'b1101111), .eq(comparator_3_eq));  // open: gt, lt
  Comparator #(.width(7)) comparator_4 (.a(keyboard), .b(7'b1101100), .eq(comparator_4_eq));  // open: gt, lt
  buf or_3 (or_3_out, restart);  // OR_Gate
  assign bot = shifter_1_out | dmx_y_cord | shifter_2_out;  // OR_Gate or_4, 16 bits wide
  or or_5 (or_5_out, comparator_2_eq, restart);
  not not_1 (not_1_out, restart);
  or or_6 (or_6_out, comparator_1_eq, restart, comparator_2_eq);
  or or_7 (or_7_out, comparator_4_eq, restart);
  not not_2 (not_2_out, restart);
  or or_8 (or_8_out, comparator_3_eq, restart, comparator_4_eq);
  // Probe on counter_3_q
  Counter #(.width(4), .max('hd), .ongoal("stay")) counter_3 (
    .load(or_5_out), .D(4'b0111), .count(not_1_out), .Q(counter_3_q), .clk(or_6_out));  // open: carry, clr
  Decoder #(.select(4)) decoder_2 (
    .out0(middle_rocket_pixel_left[1]), .out1(middle_rocket_pixel_left[2]),
    .out2(middle_rocket_pixel_left[3]), .out3(middle_rocket_pixel_left[4]),
    .out4(middle_rocket_pixel_left[5]), .out5(middle_rocket_pixel_left[6]),
    .out6(middle_rocket_pixel_left[7]), .out7(middle_rocket_pixel_left[8]),
    .out8(middle_rocket_pixel_left[9]), .out9(middle_rocket_pixel_left[10]),
    .out10(middle_rocket_pixel_left[11]), .out11(middle_rocket_pixel_left[12]),
    .out12(middle_rocket_pixel_left[13]), .out13(middle_rocket_pixel_left[14]), .sel(counter_3_q));  // open: out14, out15, en
  Counter #(.width(4), .max('hd), .ongoal("stay")) counter_4 (
    .load(or_7_out), .D(4'b0111), .count(not_2_out), .Q(counter_4_q), .clk(or_8_out));  // open: carry, clr
  Decoder #(.select(4)) decoder_3 (
    .out0(decoder_3_out0[1]), .out1(decoder_3_out0[2]), .out2(decoder_3_out0[3]), .out3(decoder_3_out0[4]),
    .out4(decoder_3_out0[5]), .out5(decoder_3_out0[6]), .out6(decoder_3_out0[7]), .out7(decoder_3_out0[8]),
    .out8(decoder_3_out0[9]), .out9(decoder_3_out0[10]), .out10(decoder_3_out0[11]),
    .out11(decoder_3_out0[12]), .out12(decoder_3_out0[13]), .out13(decoder_3_out0[14]), .sel(counter_4_q));  // open: out14, out15, en
  // Probe on racket2
  // Probe on player1
  Shifter #(.width(16)) shifter_3 (.in({1'b0, middle_rocket_pixel_left, 1'b0}), .\dist (4'b0001), .out(shifter_3_out));
  Shifter #(.width(16), .shift("lr")) shifter_4 (
    .in({1'b0, middle_rocket_pixel_left, 1'b0}), .\dist (4'b0001), .out(shifter_4_out));
  Shifter #(.width(16)) shifter_5 (.in({1'b0, decoder_3_out0, 1'b0}), .\dist (4'b0001), .out(shifter_5_out));
  Shifter #(.width(16), .shift("lr")) shifter_6 (
    .in({1'b0, decoder_3_out0, 1'b0}), .\dist (4'b0001), .out(shifter_6_out));
  not not_3 (not_3_out, swap_x_direction_right_wall);
  Comparator #(.width(5)) comparator_5 (.a(dmx_x_cord), .b(5'b11101), .eq(comparator_5_eq));  // open: gt, lt
  not not_4 (not_4_out, swap_x_direction_left_wall);
  Comparator #(.width(5)) comparator_6 (.a(dmx_x_cord), .b({5{1'b0}}), .eq(comparator_6_eq));  // open: gt, lt
  Comparator #(.width(5)) comparator_7 (.a(dmx_x_cord), .b(5'b11101), .eq(comparator_7_eq));  // open: gt, lt
  not not_5 (not_5_out, swap_x_direction_right_wall);
  Comparator #(.width(5)) comparator_8 (.a(dmx_x_cord), .b({5{1'b0}}), .eq(comparator_8_eq));  // open: gt, lt
  not not_6 (not_6_out, swap_x_direction_left_wall);
  and and_1 (and_1_out, not_3_out, comparator_5_eq);
  and and_2 (and_2_out, not_4_out, comparator_6_eq);
  Transistor #(.\type ("n")) transistor_1 (.in(not_5_out), .out(transistor_1_out), .gate(comparator_7_eq));
  Pull_Resistor pull_resistor_1 (.node(transistor_1_out));
  Pull_Resistor pull_resistor_2 (.node(pull_resistor_2_node));
  Transistor #(.\type ("n")) transistor_2 (.in(not_6_out), .out(pull_resistor_2_node), .gate(comparator_8_eq));
  assign player1 = shifter_3_out | {1'b0, middle_rocket_pixel_left, 1'b0} | shifter_4_out;  // OR_Gate or_9, 16 bits wide
  assign player2 = shifter_5_out | {1'b0, decoder_3_out0, 1'b0} | shifter_6_out;  // OR_Gate or_10, 16 bits wide
  comp_y_cord comp_y_cord_1 (.in_1(racket2), .in_2(cord2), .in_3(isDown), .out_4(comp_y_cord_1_out_4));
  or or_11 (swap_x_direction_right_wall, comp_y_cord_1_out_4, fail2);
  comp_y_cord comp_y_cord_2 (.in_1(player1), .in_2(cord1), .in_3(isDown), .out_4(comp_y_cord_2_out_4));
  or or_12 (swap_x_direction_left_wall, comp_y_cord_2_out_4, fail1);
  // OR_Gate or_13 has open pins: in0=and_1_out, in1=and_2_out, out=open
  or or_14 (lose, transistor_1_out, pull_resistor_2_node);
  Counter #(.width(4), .max('hf)) counter_5 (
    .load(undriven_3), .D(undriven_2), .count(undriven), .clk(undriven_4));  // open: Q, carry, clr
  // Probe on keyboard
  // Probe on keyboard
  Comparator #(.width(7)) comparator_9 (.a(keyboard), .b(7'b1110000), .eq(comparator_9_eq));  // open: gt, lt
  Comparator #(.width(7)) comparator_10 (.a(keyboard), .b(7'b1110010), .eq(comparator_10_eq));  // open: gt, lt
  T_Flip_Flop t_ff_1 (.clk(comparator_9_eq), .T(comparator_9_eq), .Q(pause));  // open: Qn, preset, reset, en
  T_Flip_Flop t_ff_2 (.clk(comparator_10_eq), .T(comparator_10_eq), .Q(restart));  // open: Qn, preset, reset, en
  // Probe on dmx_x_cord
  Counter #(.ongoal("continue")) counter_6 (
    .Q(counter_6_q), .clk(fail1), .clr(restart));  // open: load, D, count, carry
  Counter #(.ongoal("continue")) counter_7 (
    .Q(counter_7_q), .clk(fail2), .clr(restart));  // open: load, D, count, carry
  Clock clock_1 (.out(kpower));
  // Probe on keyboard
  // Probe on counter_6_q
  bcd bcd_1 (._8bit_Input(counter_6_q), .BCD_Output(p2_score));
  // Probe on counter_7_q
  bcd bcd_2 (._8bit_Input(counter_7_q), .BCD_Output(p1_score));
  Multiplexer #(.width(8)) multiplexer_34 (
    .in0(8'h60), .in1({8{1'b0}}), .out(multiplexer_34_out), .sel(pause));  // open: en
  Comparator #(.width(7)) comparator_11 (.a(keyboard), .b(7'b1100010), .eq(comparator_11_eq));  // open: gt, lt
  nor nor_1 (fail1, dmx_x_cord[0], dmx_x_cord[1], dmx_x_cord[2], dmx_x_cord[3], dmx_x_cord[4]);
  and and_3 (fail2, dmx_x_cord[0], dmx_x_cord[1], dmx_x_cord[2], dmx_x_cord[3], dmx_x_cord[4]);
  frequency_divider frequency_divider_1 (.IN(kpower), .OUT(power), .n(multiplexer_34_out));
  T_Flip_Flop t_ff_3 (.clk(comparator_11_eq), .T(comparator_11_eq), .Q(bot_enabled));  // open: Qn, preset, reset, en

  // Other names for the same wires on the sheet: racket1[15:0] = player1

  // Notes on the sheet:
  //   SCORE
  //   Player 1
  //   SCORE
  //   Player 2
  //   Inputs
  //   Player 1 - W and S
  //   Player 2 - O and L
  //   Pause - P
  //   Restart - R
  //   Bot - B
  //   PLAYER_1
  //   PLAYER_2
  //   движение по оси y
  //   движение по оси x
  //   BOT (Skynet in future)
  //   Keyboard input
  //   Keyboard input
  //   можно воткнуть сюда регистр
  //   если попадание: правая стенка
  //   если попадание: левая стенка
  //   неработающие варианты проверки на столкновение
  //   Data
  //   Count
  //   Load
  //   Keyboard input
  //   Load
  //   Clock
  //   Count
  //   1       0 — load from Data at next Clock trigger 
  //   0       1 — increments cur reg value at next clck trg
  //   1       1 — dec cur reg val at next clck trg
  //   Goal check
  //   Power
  //   Score count and print
endmodule

// ||
module comp_y_cord (
  input  [15:0] in_1,
  input  [15:0] in_2,
  input  in_3,
  output out_4
);

  wire and_1_out, and_2_out, and_3_out, and_4_out, and_5_out, and_6_out, and_7_out, and_8_out, and_9_out,
       and_10_out, and_11_out, and_12_out, and_13_out, and_14_out, and_15_out, and_16_out, and_17_out,
       and_18_out, and_19_out, and_20_out, and_21_out, and_22_out, and_23_out, and_24_out, and_25_out,
       and_26_out, and_27_out, and_28_out, and_29_out, and_30_out, and_31_out, and_32_out, and_33_out,
       and_34_out, and_35_out, and_36_out, and_37_out, and_38_out, and_39_out, and_40_out, and_41_out,
       and_42_out, and_43_out, and_44_out, or_1_out, or_2_out, or_3_out, or_4_out, or_5_out;

  and and_1 (and_1_out, in_1[0], in_2[0]);
  and and_2 (and_2_out, in_1[1], in_2[1]);
  and and_3 (and_3_out, in_1[2], in_2[2]);
  and and_4 (and_4_out, in_1[3], in_2[3]);
  and and_5 (and_5_out, in_1[4], in_2[4]);
  and and_6 (and_6_out, in_1[5], in_2[5]);
  and and_7 (and_7_out, in_1[6], in_2[6]);
  and and_8 (and_8_out, in_1[7], in_2[7]);
  and and_9 (and_9_out, in_1[8], in_2[8]);
  and and_10 (and_10_out, in_1[9], in_2[9]);
  and and_11 (and_11_out, in_1[10], in_2[10]);
  and and_12 (and_12_out, in_1[11], in_2[11]);
  and and_13 (and_13_out, in_1[12], in_2[12]);
  and and_14 (and_14_out, in_1[13], in_2[13]);
  and and_15 (and_15_out, in_1[14], in_2[14]);
  and and_16 (and_16_out, in_1[15], in_2[15]);
  and and_17 (and_17_out, in_2[2], in_1[1]);
  and and_18 (and_18_out, in_2[3], in_1[2]);
  and and_19 (and_19_out, in_2[4], in_1[3]);
  and and_20 (and_20_out, in_2[5], in_1[4]);
  and and_21 (and_21_out, in_2[6], in_1[5]);
  and and_22 (and_22_out, in_2[7], in_1[6]);
  and and_23 (and_23_out, in_2[8], in_1[7]);
  and and_24 (and_24_out, in_2[9], in_1[8]);
  and and_25 (and_25_out, in_2[10], in_1[9]);
  and and_26 (and_26_out, in_2[11], in_1[10]);
  and and_27 (and_27_out, in_2[12], in_1[11]);
  and and_28 (and_28_out, in_2[13], in_1[12]);
  and and_29 (and_29_out, in_2[14], in_1[13]);
  and and_30 (and_30_out, in_2[15], in_1[14]);
  and and_31 (and_31_out, in_2[0], in_1[1]);
  and and_32 (and_32_out, in_2[1], in_1[2]);
  and and_33 (and_33_out, in_2[2], in_1[3]);
  and and_34 (and_34_out, in_2[3], in_1[4]);
  and and_35 (and_35_out, in_2[4], in_1[5]);
  and and_36 (and_36_out, in_2[5], in_1[6]);
  and and_37 (and_37_out, in_2[6], in_1[7]);
  and and_38 (and_38_out, in_2[7], in_1[8]);
  and and_39 (and_39_out, in_2[8], in_1[9]);
  and and_40 (and_40_out, in_2[9], in_1[10]);
  and and_41 (and_41_out, in_2[10], in_1[11]);
  and and_42 (and_42_out, in_2[11], in_1[12]);
  and and_43 (and_43_out, in_2[12], in_1[13]);
  and and_44 (and_44_out, in_2[13], in_1[14]);
  or or_1 (or_1_out, and_1_out, and_2_out, and_3_out, and_4_out, and_5_out, and_6_out, and_7_out, and_8_out, and_9_out, and_10_out, and_11_out, and_12_out, and_13_out, and_14_out, and_15_out, and_16_out);
  or or_2 (or_2_out, and_17_out, and_18_out, and_19_out, and_20_out, and_21_out, and_22_out, and_23_out, and_24_out, and_25_out, and_26_out, and_27_out, and_28_out, and_29_out);
  or or_3 (or_3_out, and_31_out, and_32_out, and_33_out, and_34_out, and_35_out, and_36_out, and_37_out, and_38_out, and_39_out, and_40_out, and_41_out, and_42_out, and_43_out, and_44_out);
  or or_4 (or_4_out, or_1_out, or_2_out);
  or or_5 (or_5_out, or_1_out, or_3_out);
  Multiplexer multiplexer_1 (.in0(or_5_out), .in1(or_4_out), .out(out_4), .sel(in_3));  // open: en

  // Other names for the same wires on the sheet: _1_down = in_3; _0 = in_2[0]; ball_cord_y[15:0] = in_2; _1 = in_2[1];
  //   _2 = in_2[2]; _3 = in_2[3]; _4 = in_2[4]; _5 = in_2[5]; _6 = in_2[6]; _7 = in_2[7]; _8 = in_2[8]; _9 = in_2[9];
  //   _10 = in_2[10]; _11 = in_2[11]; _12 = in_2[12]; _13 = in_2[13]; _14 = in_2[14]; _15 = in_2[15];
  //   rock_cord_y[15:0] = in_1

  // Notes on the sheet:
  //   ракетка
  //   шарик
  //   сверху вниз
  //   снизу вверх
endmodule

module parseScore (
  input  [7:0] in_1,
  output [3:0] out_2,
  output [3:0] out_3,
  output [3:0] out_4
);

  wire [7:0] divider_1_out, divider_2_out, multiplier_1_out, multiplier_2_out, subtractor_1_out,
       subtractor_2_out;

  // Probe on in_1
  // Probe on divider_1_out
  Divider divider_1 (.a(in_1), .b(8'ha), .out(divider_1_out));  // open: upper, rem
  Divider divider_2 (.a(divider_1_out), .b(8'ha), .out(divider_2_out));  // open: upper, rem
  Multiplier multiplier_1 (.a(divider_1_out), .b(8'ha), .out(multiplier_1_out));  // open: cin, cout
  // Probe on multiplier_1_out
  // Probe on multiplier_2_out
  Multiplier multiplier_2 (.a(divider_2_out), .b(8'ha), .out(multiplier_2_out));  // open: cin, cout
  Bit_Extender #(.out_width(4)) bit_extender_1 (.in(divider_2_out), .out(out_2));
  Subtractor subtractor_1 (.a(in_1), .b(multiplier_1_out), .out(subtractor_1_out));  // open: bin, bout
  // Probe on out_2
  // Probe on subtractor_2_out
  Subtractor subtractor_2 (.a(divider_1_out), .b(multiplier_2_out), .out(subtractor_2_out));  // open: bin, bout
  // Probe on subtractor_1_out
  Bit_Extender #(.out_width(4)) bit_extender_2 (.in(subtractor_2_out), .out(out_3));
  Bit_Extender #(.out_width(4)) bit_extender_3 (.in(subtractor_1_out), .out(out_4));

  // Notes on the sheet:
  //   OBSOLETE
  //   as of v0.1.3
endmodule

module ai_right_rocket (
  input  [15:0] in_1,
  input  [15:0] in_2
);


  // Notes on the sheet:
  //   y_cord_of_ball
  //   y_cord_of_rocket
endmodule

module test (
);

  wire comparator_1_eq, comparator_2_eq, or_1_out, power, restart;
  wire [2:0] counter_1_q;
  wire [6:0] keyboard;
  wire [7:0] demultiplexer_1_out1, demultiplexer_1_out2, demultiplexer_1_out3, demultiplexer_1_out4,
       demultiplexer_1_out5, demultiplexer_1_out6, demultiplexer_1_out7, middle_rocket_pixel_left, rocket1,
       shifter_1_out, shifter_2_out;

  Keyboard #(.buflen(1)) keyboard_1 (.clk(power), .data(keyboard));  // open: re, clr, avail
  Clock clock_1 (.out(power));
  Button button_1 (.out(restart));
  // Probe on keyboard
  // Probe on keyboard
  Comparator #(.width(7)) comparator_1 (.a(keyboard), .b(7'b1110111), .eq(comparator_1_eq));  // open: gt, lt
  Comparator #(.width(7)) comparator_2 (.a(keyboard), .b(7'b1110011), .eq(comparator_2_eq));  // open: gt, lt
  DotMatrix #(.matrixcols(8), .matrixrows(8)) dotmatrix_1 (
    .col0(rocket1), .col1(demultiplexer_1_out1), .col2(demultiplexer_1_out2), .col3(demultiplexer_1_out3),
    .col4(demultiplexer_1_out4), .col5(demultiplexer_1_out5), .col6(demultiplexer_1_out6),
    .col7(demultiplexer_1_out7));
  Demultiplexer #(.select(3), .width(8)) demultiplexer_1 (
    .out0(rocket1), .out1(demultiplexer_1_out1), .out2(demultiplexer_1_out2), .out3(demultiplexer_1_out3),
    .out4(demultiplexer_1_out4), .out5(demultiplexer_1_out5), .out6(demultiplexer_1_out6),
    .out7(demultiplexer_1_out7));  // open: in, sel, en
  Counter #(.width(3), .max('h7)) counter_1 (
    .load(comparator_2_eq), .Q(counter_1_q), .clk(or_1_out), .clr(restart));  // open: D, count, carry
  or or_1 (or_1_out, comparator_1_eq, comparator_2_eq);
  Decoder #(.select(3)) decoder_1 (
    .out0(middle_rocket_pixel_left[0]), .out1(middle_rocket_pixel_left[1]),
    .out2(middle_rocket_pixel_left[2]), .out3(middle_rocket_pixel_left[3]),
    .out4(middle_rocket_pixel_left[4]), .out5(middle_rocket_pixel_left[5]),
    .out6(middle_rocket_pixel_left[6]), .out7(middle_rocket_pixel_left[7]), .sel(counter_1_q));  // open: en
  Shifter shifter_1 (.in(middle_rocket_pixel_left), .\dist (3'b001), .out(shifter_1_out));
  Shifter #(.shift("lr")) shifter_2 (.in(middle_rocket_pixel_left), .\dist (3'b001), .out(shifter_2_out));
  assign rocket1 = shifter_1_out | middle_rocket_pixel_left | shifter_2_out;  // OR_Gate or_2, 8 bits wide

  // Notes on the sheet:
  //   Inputs
  //   w, s // o, l
endmodule

module frequency_divider (
  input  [7:0] n,
  input  IN,
  output OUT
);

  wire comparator_1_eq, comparator_1_lt, or_1_out;
  wire [7:0] counter_1_q;

  Counter counter_1 (.count(IN), .Q(counter_1_q), .clk(IN), .clr(or_1_out));  // open: load, D, carry
  Comparator #(.mode("unsigned")) comparator_1 (
    .a(n), .b(counter_1_q), .eq(comparator_1_eq), .lt(comparator_1_lt));  // open: gt
  or or_1 (or_1_out, comparator_1_eq, comparator_1_lt);
  T_Flip_Flop t_ff_1 (.clk(or_1_out), .T(or_1_out), .Q(OUT));  // open: Qn, preset, reset, en
endmodule

module bcd (
  input  [7:0] _8bit_Input,
  output [11:0] BCD_Output
);

  wire [3:0] bcd_helper_1_out, bcd_helper_2_out, bcd_helper_3_out, bcd_helper_4_out, bcd_helper_5_out,
       bcd_helper_6_out, bcd_helper_7_out, bcd_helper_8_out, bcd_helper_9_out, bcd_helper_10_out,
       bcd_helper_11_out, bcd_helper_12_out, bcd_helper_13_out, bcd_helper_14_out, bcd_helper_15_out,
       bcd_helper_16_out, bcd_helper_17_out, bcd_helper_18_out;
  wire [3:3] bcd_helper_21_out;

  // Probe on _8bit_Input
  bcd_helper bcd_helper_1 (.inp({3'b000, _8bit_Input[7]}), .out(bcd_helper_1_out));
  bcd_helper bcd_helper_2 (.inp(4'b0000), .out(bcd_helper_2_out));
  bcd_helper bcd_helper_3 (.inp(4'b0000), .out(bcd_helper_3_out));
  bcd_helper bcd_helper_4 (.inp({bcd_helper_1_out[2:0], _8bit_Input[6]}), .out(bcd_helper_4_out));
  bcd_helper bcd_helper_5 (.inp({bcd_helper_2_out[2:0], bcd_helper_1_out[3]}), .out(bcd_helper_5_out));
  bcd_helper bcd_helper_6 (.inp({bcd_helper_3_out[2:0], bcd_helper_2_out[3]}), .out(bcd_helper_6_out));
  bcd_helper bcd_helper_7 (.inp({bcd_helper_4_out[2:0], _8bit_Input[5]}), .out(bcd_helper_7_out));
  bcd_helper bcd_helper_8 (.inp({bcd_helper_5_out[2:0], bcd_helper_4_out[3]}), .out(bcd_helper_8_out));
  bcd_helper bcd_helper_9 (.inp({bcd_helper_6_out[2:0], bcd_helper_5_out[3]}), .out(bcd_helper_9_out));
  bcd_helper bcd_helper_10 (.inp({bcd_helper_7_out[2:0], _8bit_Input[4]}), .out(bcd_helper_10_out));
  bcd_helper bcd_helper_11 (.inp({bcd_helper_8_out[2:0], bcd_helper_7_out[3]}), .out(bcd_helper_11_out));
  bcd_helper bcd_helper_12 (.inp({bcd_helper_9_out[2:0], bcd_helper_8_out[3]}), .out(bcd_helper_12_out));
  bcd_helper bcd_helper_13 (.inp({bcd_helper_10_out[2:0], _8bit_Input[3]}), .out(bcd_helper_13_out));
  bcd_helper bcd_helper_14 (.inp({bcd_helper_11_out[2:0], bcd_helper_10_out[3]}), .out(bcd_helper_14_out));
  bcd_helper bcd_helper_15 (.inp({bcd_helper_12_out[2:0], bcd_helper_11_out[3]}), .out(bcd_helper_15_out));
  bcd_helper bcd_helper_16 (.inp({bcd_helper_13_out[2:0], _8bit_Input[2]}), .out(bcd_helper_16_out));
  bcd_helper bcd_helper_17 (.inp({bcd_helper_14_out[2:0], bcd_helper_13_out[3]}), .out(bcd_helper_17_out));
  bcd_helper bcd_helper_18 (.inp({bcd_helper_15_out[2:0], bcd_helper_14_out[3]}), .out(bcd_helper_18_out));
  bcd_helper bcd_helper_19 (.inp({bcd_helper_16_out[2:0], _8bit_Input[1]}), .out(BCD_Output[4:1]));
  bcd_helper bcd_helper_20 (.inp({bcd_helper_17_out[2:0], bcd_helper_16_out[3]}), .out(BCD_Output[8:5]));
  bcd_helper bcd_helper_21 (
    .inp({bcd_helper_18_out[2:0], bcd_helper_17_out[3]}), .out({bcd_helper_21_out[3], BCD_Output[11:9]}));
  // Probe on BCD_Output[11:8]
  // Probe on {BCD_Output[3:1], _8bit_Input[0]}
  // Probe on BCD_Output[7:4]

  assign BCD_Output[0] = _8bit_Input[0];

  // Notes on the sheet:
  //   The double dable algorithm
endmodule

module bcd_helper (
  input  [3:0] inp,
  output [3:0] out
);

  wire comparator_1_eq, comparator_1_lt, or_1_out;
  wire [3:0] adder_1_out;

  // Probe on inp
  Adder #(.width(4)) adder_1 (.a(4'b0011), .b(inp), .out(adder_1_out));  // open: cin, cout
  Comparator #(.width(4), .mode("unsigned")) comparator_1 (
    .a(4'b0101), .b(inp), .eq(comparator_1_eq), .lt(comparator_1_lt));  // open: gt
  or or_1 (or_1_out, comparator_1_eq, comparator_1_lt);
  Multiplexer #(.width(4)) multiplexer_1 (.in0(inp), .in1(adder_1_out), .out(out), .sel(or_1_out));  // open: en
endmodule
